// Logisim project PWM.circ as structural Verilog: 5 circuits, main circuit PWM_Servo
module PWM_Servo (
  input  [7:0] Angle,
  input  EN_HT,
  input  clk,
  input  Reset,
  output SERVO_OUT
);

  wire [25:0] Servo_Mapper_1_out_26b;

  Servo_Mapper Servo_Mapper_1 (.In_8b(Angle), .Out_26b(Servo_Mapper_1_out_26b));
  PWM_Base PWM_Base_1 (
    .High_Time(Servo_Mapper_1_out_26b), .EN_HT(EN_HT), .Period(26'h1312d00), .EN_P(1'b1), .clk(clk),
    .Reset(Reset), .PWM_OUT(SERVO_OUT));

  // Notes on the sheet:
  //   20[ms]
endmodule

module PWM_Motor (
  input  [7:0] High,
  input  En_H,
  input  [7:0] Period,
  input  En_P,
  input  clk,
  input  Reset,
  output MOTOR_OUT
);

  wire [25:0] Motor_Mapper_1_out_26b, Motor_Mapper_2_out_26b;

  Motor_Mapper Motor_Mapper_1 (.In_8b(High), .Out_26b(Motor_Mapper_1_out_26b));
  Motor_Mapper Motor_Mapper_2 (.In_8b(Period), .Out_26b(Motor_Mapper_2_out_26b));
  PWM_Base PWM_Base_1 (
    .High_Time(Motor_Mapper_1_out_26b), .EN_HT(En_H), .Period(Motor_Mapper_2_out_26b), .EN_P(En_P),
    .clk(clk), .Reset(Reset), .PWM_OUT(MOTOR_OUT));
endmodule

module PWM_Base (
  input  [25:0] High_Time,
  input  EN_HT,
  input  [25:0] Period,
  input  EN_P,
  input  clk,
  input  Reset,
  output PWM_OUT
);

  wire comparator_1_eq, comparator_1_gt, or_1_out;
  wire [25:0] cpt, ht, p;

  Register #(.width(26)) register_1 (.D(High_Time), .en(EN_HT), .clk(clk), .Q(ht), .clr(Reset));
  Register #(.width(26)) register_2 (.D(Period), .en(EN_P), .clk(clk), .Q(p), .clr(Reset));
  Comparator #(.width(26), .mode("unsigned")) comparator_1 (
    .a(cpt), .b(p), .gt(comparator_1_gt), .eq(comparator_1_eq));  // open: lt
  Counter #(.width(26), .max('h3ffffff)) counter_1 (
    .clr(or_1_out), .clk(clk), .Q(cpt));  // open: load, up, count, D, carry
  or or_1 (or_1_out, Reset, comparator_1_gt, comparator_1_eq);
  Comparator #(.width(26), .mode("unsigned")) comparator_2 (.a(cpt), .b(ht), .lt(PWM_OUT));  // open: gt, eq

  // Other names for the same wires on the sheet: R = Reset
endmodule

module Servo_Mapper (
  input  [7:0] In_8b,
  output [25:0] Out_26b
);

  Adder #(.width(26)) adder_1 (.a({10'h1, In_8b, {8{1'b0}}}), .b(26'hca70), .out(Out_26b));  // open: cin, cout
endmodule

module Motor_Mapper (
  input  [7:0] In_8b,
  output [25:0] Out_26b
);

  Adder #(.width(26)) adder_1 (.a({In_8b, {18{1'b0}}}), .b(26'hca70), .out(Out_26b));  // open: cin, cout
endmodule
