// Logisim project Timer.circ as structural Verilog: 1 circuit, main circuit Timer
module Timer (
  input  [7:0] Sleep_Time,
  input  EN,
  input  CLK,
  input  Reset,
  output [7:0] TimeOut
);

  wire count, or_1_out;
  wire [7:0] val;
  wire [25:0] counter_1_q;

  Register register_1 (.D(Sleep_Time), .en(EN), .clk(CLK), .Q(val), .clr(Reset));
  Counter #(.width(26), .max('h3ffffff)) counter_1 (
    .clr(or_1_out), .count(count), .clk(CLK), .Q(counter_1_q));  // open: load, up, D, carry
  or or_1 (or_1_out, Reset, EN);
  Comparator #(.width(26), .mode("unsigned")) comparator_1 (
    .a(counter_1_q), .b({val, {18{1'b1}}}), .eq(TimeOut[0]));  // open: gt, lt
  not not_1 (count, TimeOut[0]);

  assign TimeOut[7:1] = {7{1'b0}};

  // Other names for the same wires on the sheet: ld = EN; R = Reset
endmodule
